# Fritzing sketch ArDNC (saved by Fritzing 0.9.2b)
circuit board: 9.07451cm x 7.41243cm

parts:
  Arduino_Uno = Arduino Uno (Rev3)
  Display = Adafruit RGB LCD Shield [part_number="Adafruit #714 and #716"]
  23201a = IC, SIP package, 12 pins [chip_label=23201a]
  SD_Reader = IC, SIP package, 10 pins [chip_label=SD]
  J-A-1 = male pin header, 6 pins [form="♂ (male)"]
  J-B-1 = male pin header, 6 pins [form="♂ (male)"]
  JC-A-2 = female pin header, 6 pins [form="♀ (female)"]
  JC-A-1 = female pin header, 6 pins [form="♀ (female)"]
  JC-B-2 = female pin header, 6 pins [form="♀ (female)"]
  JC-B-1 = female pin header, 6 pins [form="♀ (female)"]
  J-A-2 = male pin header, 6 pins [form="♂ (male)"]
  J-B-2 = male pin header, 6 pins [form="♂ (male)"]
  J-1-1 = male pin header, 6 pins [form="♂ (male)"]
  J-2-1 = male pin header, 6 pins [form="♂ (male)"]
  JC-1-2 = female pin header, 6 pins [form="♀ (female)"]
  JC-2-2 = female pin header, 6 pins [form="♀ (female)"]
  JC-1-1 = female pin header, 6 pins [form="♀ (female)"]
  JC-2-1 = female pin header, 6 pins [form="♀ (female)"]
  J-1-2 = male pin header, 6 pins [form="♂ (male)"]
  J-2-2 = male pin header, 6 pins [form="♂ (male)"]

nets:
  N1: Arduino_Uno.A4/SDA, Display.SDA
  N2: Arduino_Uno.A5/SCL, Display.SCL
  N3: Arduino_Uno.D10_PWM/SS, J-A-1.pin3
  N4: Arduino_Uno.D11_PWM/MOSI, J-A-1.pin4
  N5: Arduino_Uno.D12/MISO, J-A-1.pin6
  N6: Arduino_Uno.D13/SCK, J-A-1.pin5
  GND: Arduino_Uno.GND, Display.GND, J-B-1.pin5, J-2-1.pin2
  N7: Arduino_Uno.D0/RX, J-2-1.pin4
  N8: Arduino_Uno.D1/TX, J-2-1.pin5
  N9: Arduino_Uno.RESET, Display.RESET
  N10: Arduino_Uno.3V3, J-B-1.pin4
  5V: Arduino_Uno.5V, Display.+5V, J-1-1.pin3
  N11: 23201a.pin2, J-2-2.pin5
  N12: 23201a.pin3, J-2-2.pin4
  N13: 23201a.pin5, J-2-2.pin2
  N14: 23201a.pin10, J-1-2.pin3
  N15: SD_Reader.pin1, J-B-2.pin5
  N16: SD_Reader.pin2, J-B-2.pin4
  N17: SD_Reader.pin6, J-A-2.pin6
  N18: SD_Reader.pin7, J-A-2.pin5
  N19: SD_Reader.pin8, J-A-2.pin4
  N20: SD_Reader.pin9, J-A-2.pin3
  N21: JC-A-2.pin1, JC-A-1.pin1
  N22: JC-A-2.pin2, JC-A-1.pin2
  N23: JC-A-2.pin3, JC-A-1.pin3
  N24: JC-A-2.pin4, JC-A-1.pin4
  N25: JC-A-2.pin5, JC-A-1.pin5
  N26: JC-A-2.pin6, JC-A-1.pin6
  N27: JC-B-2.pin1, JC-B-1.pin1
  N28: JC-B-2.pin2, JC-B-1.pin2
  N29: JC-B-2.pin3, JC-B-1.pin3
  N30: JC-B-2.pin4, JC-B-1.pin4
  N31: JC-B-2.pin5, JC-B-1.pin5
  N32: JC-B-2.pin6, JC-B-1.pin6
  N33: JC-1-2.pin1, JC-1-1.pin1
  N34: JC-1-2.pin2, JC-1-1.pin2
  N35: JC-1-2.pin3, JC-1-1.pin3
  N36: JC-1-2.pin4, JC-1-1.pin4
  N37: JC-1-2.pin5, JC-1-1.pin5
  N38: JC-1-2.pin6, JC-1-1.pin6
  N39: JC-2-2.pin1, JC-2-1.pin1
  N40: JC-2-2.pin2, JC-2-1.pin2
  N41: JC-2-2.pin3, JC-2-1.pin3
  N42: JC-2-2.pin4, JC-2-1.pin4
  N43: JC-2-2.pin5, JC-2-1.pin5
  N44: JC-2-2.pin6, JC-2-1.pin6

custom parts:
  Adafruit RGB LCD Shield: This new Adafruit shield makes it easy to use a 16x2 Character LCD. We really like the RGB LCDs we stock in the shop both the RGB negative and RGB positive. Unfortunately, these LCDs do require quite a few digital pins, 6 to control the LCD and then another 3 to control the RGB backlight for a total of 9 pins. That's half of the pins available on a classic Arduino! With this in mind, we wanted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
